# Fritzing sketch schematic (saved by Fritzing 0.9.3b)
breadboards: 1

parts:
  Part3 = Real Time Clock Module - DS1307 RTC Breakout Board
  LED1 = LED - 3mm [color="Red (633nm)" package="3 mm [THT]"]
  LED2 = LED - 3mm [color="Blue (430nm)" package="3 mm [THT]"]
  S3 = Pushbutton [part_number=MODE_SW package="[SMD]"]
  S1 = Pushbutton [part_number=MINUS_SW package="[THT]"]
  Grove1 = Grove 4 Digit Display [part_number="Clock display"]
  R1 = Resistor [tolerance=±5% resistance=470 package=THT]
  R2 = Resistor [tolerance=±5% resistance=220 package=THT]
  S2 = Pushbutton [part_number=PLUS_SW package="[SMD]"]
  Part4 = Arduino Nano (Rev3.0) (ICSP)

nets:
  5V: Part3.5V, Grove1.VCC, Part4.5V
  GND: Part3.GND, LED1.cathode, LED2.cathode, S3.Pin_1, S3.Pin_2, S1.Pin_1, S1.Pin_2, Grove1.GND, S2.Pin_1, S2.Pin_2, Part4.GND
  N1: Part3.SQW, Part4.D3
  N2: Part3.SCL, Part4.A5
  N3: Part3.SDA, Part4.A4
  N4: LED1.anode, R2.Pin_1
  N5: LED2.anode, R1.Pin_1
  N6: S3.Pin_3, S3.Pin_4, Part4.D8
  N7: S1.Pin_3, S1.Pin_4, Part4.D9
  N8: Grove1.DIO, Part4.D12/MISO
  N9: Grove1.CLK, Part4.D11/MOSI
  N10: R1.Pin_0, Part4.D6
  N11: R2.Pin_0, Part4.D7
  N12: S2.Pin_3, S2.Pin_4, Part4.D10
